# Fritzing sketch led nova (saved by Fritzing 0.9.4)
circuit board: 4.5cm x 4.5cm
breadboards: 1

parts:
  Q1 = npn-Powertransistor [part_number=120 package="TO220 [THT]"]
  Q2 = npn-Powertransistor [part_number=120 package="TO220 [THT]"]
  Q3 = npn-Powertransistor [part_number=120 package="TO220 [THT]"]
  RGB_Strip_LED1 = RGB Strip LED
  IC4 = Voltage Regulator [package=78xxl]
  C15 = Electrolytic Capacitor [capacitance=100nF voltage=16V package="100 mil [THT, electrolytic]"]
  C16 = Electrolytic Capacitor [capacitance=100nF voltage=16V package="100 mil [THT, electrolytic]"]
  S1 = Pushbutton [package="[SMD]"]
  C17 = Electrolytic Capacitor [capacitance=100µF voltage=16V package="100 mil [THT, electrolytic]"]
  U2 = atmega328 [package=dip]
  R1 = Resistor [tolerance=±5% resistance=220 package=THT]
  J1 = screw terminal, 2 pins

nets (from the pcb view):
  N1: Q1.base, U2.A5
  GND: Q1.emitter, Q2.emitter, Q3.emitter, IC4.GND, C15.+, C16.+, C17.+, U2.GND, R1.Pin_1, J1.pin2
  N2: Q2.base, U2.A4
  N3: Q3.base, U2.A3
  N4: RGB_Strip_LED1.Common_Connect#8, RGB_Strip_LED1.Red_Connect#10, RGB_Strip_LED1.Green_Connect
  N5: IC4.IN, C16.-, J1.pin1
  N6: IC4.OUT, C15.-, C17.-, U2.VCC
  N7: S1.Pin_1, S1.Pin_2, U2.D8, R1.Pin_0
  N8: S1.Pin_3, S1.Pin_4, U2.AVCC

notes:
  LMR

custom parts:
  RGB Strip LED: A tri-color Strip LED with red, green and blue. Based on LED SMD 5050 RGB Pin order: common cathode - green - red - blue

// code stored in the sketch: led nova atmega328.ino
int redPin = 3;
int greenPin = 2;
int bluePin = 1;
int pulsante = 7;

int t = 300000;

const int BUTTON_PIN = 7; 
const int SHORT_PRESS_TIME = 500; 
int lastState = LOW;  
int currentState;     
unsigned long pressedTime  = 0;
unsigned long releasedTime = 0;

void setup(){
  Serial.begin(9600);
  pinMode(BUTTON_PIN, INPUT_PULLUP);
  
  pinMode(redPin, OUTPUT);
  pinMode(greenPin, OUTPUT);
  pinMode(bluePin, OUTPUT); 
  pinMode(pulsante, INPUT);
}

void loop(){

  currentState = digitalRead(BUTTON_PIN);

    if(lastState == HIGH && currentState == LOW)        // button is pressed
    pressedTime = millis();
  else if(lastState == LOW && currentState == HIGH) { // button is released
    releasedTime = millis();

    long pressDuration = releasedTime - pressedTime;

    if( pressDuration > SHORT_PRESS_TIME )
    digitalWrite(pulsante, LOW);
    else ( loopcol);
  }

  // save the the last state
  lastState = currentState;
  
}


void SetColor(int red, int green, int blue) {
  #ifdef COMMON_ANODE
    red = 255 - red;
    green = 255 - green;
    blue = 255 - blue;
  #endif
  analogWrite(redPin, red);
  analogWrite(greenPin, green);
  analogWrite(bluePin, blue);  
}

void loopcol() {
  SetColor(10,50,100);
      delay(t);
      SetColor(255,59,44);
      delay(t);
      SetColor(146,37,165);
      delay(t);
      SetColor(248,197,55);
      delay(t);
}
